# Fritzing sketch final_circuit_strip (saved by Fritzing 0.9.3b)

parts:
  J14 = double row female pin header, 6 pins [form="♀ (female)"]
  J13 = double row female pin header, 6 pins [form="♀ (female)"]
  Part6 = Adafruit BME280
  R5 = Resistor [tolerance=±5% resistance=4.7k package="0402 [SMD]"]
  IC4 = MCP3008 8-channel 10-bit ADC [part_number=MCP3008]
  R6 = Resistor [tolerance=±5% resistance=4.7k package="0402 [SMD]"]
  Part4 = Adafruit Perma-Proto HAT [part_number="Adafruit #2314 and #2310"]

nets:
  N1: J14.pin1, Part4.N$45
  N2: J14.pin2, Part4.N$44#288
  N3: J14.pin3, Part4.N$43#283
  N4: J14.pin4, Part4.N$42#278
  N5: J14.pin5, Part4.N$41#273
  N6: J14.pin6, Part4.N$39
  N7: J13.pin1, Part4.N$10
  N8: J13.pin2, Part4.N$11#207
  N9: J13.pin3, Part4.N$12#212
  N10: J13.pin4, Part4.N$13#217
  N11: J13.pin5, Part4.N$14#222
  N12: J13.pin6, Part4.N$15#227
  3.3V: Part6.3.3V, Part4.3.3V, Part4.N$11#208, Part4.N$44#286, Part4.N$61#371, Part4.N$62#376
  GND: Part6.GND, R5.Pin_1, Part4.GND, Part4.N$12#211, Part4.N$14#221, Part4.N$42#276, Part4.N$55#341, Part4.N$59#361
  N13: Part6.SCK/SCL, Part4.SCL
  N14: Part6.SDI/SDA, Part4.SDA
  N15: R5.Pin_0, Part4.N$41#274, Part4.N$47#304
  N16: IC4.no_name_yet#1, Part4.N$1#160
  N17: IC4.no_name_yet#2, Part4.N$2
  N18: IC4.no_name_yet#3, Part4.N$3
  N19: IC4.no_name_yet#4, Part4.N$4
  N20: IC4.no_name_yet#5, Part4.N$5
  N21: IC4.no_name_yet#6, Part4.N$6
  N22: IC4.no_name_yet#7, Part4.N$8
  N23: IC4.no_name_yet#8, Part4.N$7
  N24: IC4.no_name_yet#9, Part4.N$55#344
  N25: IC4.no_name_yet#10, Part4.N$56#350
  N26: IC4.no_name_yet#11, Part4.N$57#355
  N27: IC4.no_name_yet#12, Part4.N$58#360
  N28: IC4.no_name_yet#13, Part4.N$60#370
  N29: IC4.no_name_yet#14, Part4.N$59#365
  N30: IC4.no_name_yet#15, Part4.N$61#375
  N31: IC4.no_name_yet#16, Part4.N$62#380
  N32: R6.Pin_0, Part4.N$15#229
  N33: R6.Pin_1, Part4.N$11#209
  N34: Part4.GPIO4, Part4.N$15#230
  N35: Part4.SPI_MOSI, Part4.N$57#351
  N36: Part4.SPI_MISO, Part4.N$58#356
  N37: Part4.SPI_SCLK, Part4.N$60#366
  N38: Part4.SPI_CE0, Part4.N$56#346
  N39: Part4.GPIO5, Part4.N$43#281
  N40: Part4.GPIO6, Part4.N$13#220
  N41: Part4.N$1#159, Part4.N$47#305

custom parts:
  Adafruit BME280: Bosch has stepped up their game with their new BME280 sensor, an environmental sensor with temperature, barometric pressure and humidity! This sensor is great for all sorts of weather/environmental sensing and can even be used in both I2C and SPI! This precision sensor from Bosch is the best low-cost sensing solution for measuring humidity with ±3% accuracy, barometric pressure with ±1 hPa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
  Adafruit Perma-Proto HAT: To kick off the Adafruit HAT party, we have this Perma-Proto inspired plug in daughter board. It has a grid of 0.1" prototyping soldering holes for attaching chips, resistors, LED, potentiometers and more. The holes are connected underneath with traces to mimic the solderless breadboards you're familiar. There's also long power strips for +3V, +5V and Ground connections to the Pi. Near the top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
